# Fritzing sketch Leros_bike (saved by Fritzing 0.9.3b)

parts:
  S3 = Magnetic Door Switch [package=reed_switch_plastic]
  Εξάρτημα1 = Arduino Leonardo (Rev3b)

nets:
  N1: S3.1, Εξάρτημα1.GND
  N2: S3.2, Εξάρτημα1.D2/SDA
